// Logisim project door_lock_fsm.circ as structural Verilog: 1 circuit, main circuit main
module main (
  input  Scan_D3,
  input  Scan_D2,
  input  Scan_D1,
  input  Scan_D0,
  input  Card_Present,
  input  RF_Remote,
  output OUT_S0,
  output OUT_S1,
  output OUT_S2
);

  wire and_1_out, and_2_out, and_3_out, and_4_out, and_5_out, CLK, D0_Final, D1_Final, MATCH, not_3_out,
       not_4_out, not_5_out, not_6_out, NOT_MATCH, NOT_RF_Remote, NOT_TimerDone, Q0, Q1, TimerDone,
       xnor_1_out, xnor_2_out, xnor_3_out, xnor_4_out, xor_1_out;
  wire [3:0] counter_1_q;

  Clock clock_1 (.out(CLK));
  and and_1 (and_1_out, OUT_S0, Card_Present, MATCH);
  and and_2 (and_2_out, OUT_S0, RF_Remote);
  and and_3 (and_3_out, OUT_S1, NOT_TimerDone);
  and and_4 (and_4_out, OUT_S0, Card_Present, NOT_MATCH);
  and and_5 (and_5_out, OUT_S2, NOT_RF_Remote);
  or or_1 (D0_Final, and_1_out, and_2_out, and_3_out);
  or or_2 (D1_Final, and_4_out, and_5_out);
  xnor xnor_1 (xnor_1_out, Scan_D3, 1'b0);
  xnor xnor_2 (xnor_2_out, Scan_D2, 1'b0);
  xnor xnor_3 (xnor_3_out, Scan_D1, 1'b0);
  xnor xnor_4 (xnor_4_out, Scan_D0, 1'b1);
  and and_6 (MATCH, xnor_1_out, xnor_2_out, xnor_3_out, xnor_4_out);
  Counter #(.width(4), .max('h5)) counter_1 (
    .load(OUT_S1), .count(OUT_S0), .Q(counter_1_q), .clk(CLK));  // open: D, carry, clr
  LED Access_Granted (.in(OUT_S1));
  LED Door_Unlocked (.in(OUT_S1));
  LED System_Secured (.in(OUT_S0));
  LED Alarm_Flash (.in(xor_1_out));
  xor xor_1 (xor_1_out, OUT_S2, CLK);
  not not_1 (NOT_MATCH, MATCH);
  not not_2 (NOT_RF_Remote, RF_Remote);
  Comparator #(.width(4)) comparator_1 (.a(counter_1_q), .b(4'b0101), .eq(TimerDone));  // open: gt, lt
  D_Flip_Flop FF1__MSB (.clk(CLK), .D(D1_Final), .Q(Q1));  // open: Qn, preset, en, reset
  D_Flip_Flop FF0__LSB (.clk(CLK), .D(D0_Final), .Q(Q0));  // open: Qn, preset, en, reset
  not not_3 (not_3_out, Q1);
  not not_4 (not_4_out, Q1);
  not not_5 (not_5_out, Q0);
  not not_6 (not_6_out, Q0);
  not not_7 (NOT_TimerDone, TimerDone);
  and Secured (OUT_S0, not_4_out, not_5_out);
  and Granted (OUT_S1, not_3_out, Q0);
  and Alarm (OUT_S2, Q1, not_6_out);

  // Other names for the same wires on the sheet: S0 = OUT_S0; S1 = OUT_S1; S2 = OUT_S2

  // Notes on the sheet:
  //   Auth_D3
  //   Auth_D2
  //   Auth_D1
  //   Auth_D0
endmodule
